# Fritzing sketch Diagrama (saved by Fritzing 0.9.5d)
breadboards: 1

parts:
  DHT1 = DHT11 Humitidy and Temperature Sensor
  R1 = Resistor [tolerance=±5% resistance=10k package=THT]
  Componente1 = Arduino Uno (Rev3)

nets:
  VDD: DHT1.VDD, R1.Pin_0, Componente1.5V
  N1: DHT1.DATA, R1.Pin_1, Componente1.D2
  GND: DHT1.GND, Componente1.GND

custom parts:
  DHT11 Humitidy and Temperature Sensor: DHT11 Humidity and Temperature Sensor
