# Fritzing sketch RedBot (saved by Fritzing 0.9.3b)
breadboards: 1

parts:
  Componente1 = Arduino Uno (Rev3) - ICSP  # not connected
  Componente1_2 = Arduino Uno (Rev3) - ICSP
  VCC1 = 4 x AAA Battery Mount
  Componente2 = Motor Driver 1A Dual TB6612FNG
  M1 = DC Motor
  M2 = DC Motor
  Componente3 = Bluetooth HC-05 Macho

nets:
  N1: Componente1_2.D9_PWM, Componente2.BIN2
  N2: Componente1_2.D10_PWM/SS, Componente2.BIN1
  N3: Componente1_2.D11_PWM/MOSI, Componente2.STBY
  N4: Componente1_2.D12/MISO, Componente2.AIN1
  N5: Componente1_2.D13/SCK, Componente2.AIN2
  N6: Componente1_2.D2, Componente3.TXD
  N7: Componente1_2.D3_PWM, Componente3.RXD
  N8: Componente1_2.D5_PWM, Componente2.PWMB
  N9: Componente1_2.D6_PWM, Componente2.PWMA
  VCC: Componente1_2.5V, Componente2.VCC, Componente3.VCC
  GND: Componente1_2.GND, VCC1.-, Componente2.GND, Componente3.GND
  N10: Componente1_2.VIN, VCC1.+, Componente2.VM
  N11: Componente2.B01, M1.pin_1
  N12: Componente2.B02, M1.pin_2
  N13: Componente2.A02, M2.pin_1
  N14: Componente2.A01, M2.pin_2
