# Fritzing sketch Diagrama (saved by Fritzing 0.9.3b)
breadboards: 1

parts:
  SparkFun_ESP32_Thing1 = SparkFun ESP32 Thing [part_number=DEV-13907]
  J1 = screw terminal, 3 pins
  R1 = Resistor [tolerance=±5% resistance=220 package=THT]
  Q1 = PNP-Transistor [package="TO92 [THT]"]
  R2 = Resistor [tolerance=±5% resistance=10k package=THT]

nets:
  N1: SparkFun_ESP32_Thing1.VUSB-RAW, J1.pin2, R2.Pin_0
  N2: SparkFun_ESP32_Thing1.GND, J1.pin1, Q1.C
  N3: SparkFun_ESP32_Thing1.5, R1.Pin_1
  N4: J1.pin3, Q1.E, R2.Pin_1
  N5: R1.Pin_0, Q1.B

notes:
  GND
  Vcc
  Señal

custom parts:
  SparkFun ESP32 Thing: The SparkFun ESP32 Thing is a comprehensive development platform for Espressif’s ESP32, their super-charged version of the popular ESP8266. Like the 8266, the ESP32 is a WiFi-compatible microcontroller, but to that it adds support for Bluetooth low-energy (i.e BLE, BT4.0, Bluetooth Smart), and nearly 30 I/O pins. The ESP32’s power and versatility will make it the foundation of IoT and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
