# Fritzing sketch MiniRadarDoble (saved by Fritzing 0.9.3b)
breadboards: 1

parts:
  Componente1 = Arduino Uno (Rev3)
  J1 = Basic Servo
  J2 = Basic Servo
  hc-sr1 = hc-sr04
  hc-sr2 = hc-sr04

nets:
  N1: Componente1.D9_PWM, J1.pulse
  N2: Componente1.D10_PWM/SS, J2.pulse
  N3: Componente1.D4, hc-sr2.Trig
  N4: Componente1.D5_PWM, hc-sr2.Echo
  N5: Componente1.D6_PWM, hc-sr1.Trig
  N6: Componente1.D7, hc-sr1.Echo
  VCC: Componente1.5V, J1.vcc, J2.vcc, hc-sr1.VCC, hc-sr2.VCC
  GND: Componente1.GND, J1.gnd, J2.gnd, hc-sr1.GND, hc-sr2.GND
