# Fritzing sketch BasculaDigital (saved by Fritzing 0.9.3b)
circuit board: 8.57788cm x 5.85574cm
breadboards: 1

parts:
  J1 = LOAD_CELL [package=1x03]
  Componente1 = HX711 Weighing Sensor Module
  Componente2 = SparkFun ESP8266 Thing

nets:
  N1: J1.B, Componente1.A-
  N2: J1.W, Componente1.A+
  N3: J1.R, Componente1.B+
  VCC: Componente1.VCC, Componente2.VCC
  GND: Componente1.GND, Componente2.GND
  N4: Componente1.DO/RX, Componente2.GPIO5
  N5: Componente1.CK/TX, Componente2.GPIO2
