# Fritzing sketch CalabazaInteligente (saved by Fritzing 0.9.3b)
breadboards: 1

parts:
  Componente1 = SparkFun ESP8266 Thing
  hc-sr1 = hc-sr04
  R1 = Resistor [tolerance=±5% resistance=330 package=THT]
  R2 = Resistor [tolerance=±5% resistance=330 package=THT]
  LED1 = LED - 5mm [color="Red (633nm)" package="5 mm [THT]"]
  LED2 = LED - 5mm [color="Red (633nm)" package="5 mm [THT]"]

nets:
  GND: Componente1.GND, hc-sr1.GND, R1.Pin_1, R2.Pin_1
  N1: Componente1.GPIO0, LED2.anode
  N2: Componente1.GPIO4, LED1.anode
  N3: Componente1.GPIO13, hc-sr1.Echo
  N4: Componente1.GPIO12, hc-sr1.Trig
  N5: R1.Pin_0, LED2.cathode
  N6: R2.Pin_0, LED1.cathode
