# Fritzing sketch Untitled Sketch (saved by Fritzing 0.9.3b)

parts:
  HC-SR04_Sensor_1 = HC-SR04 Ultrasonic Distance Sensor
  Componente1 = Arduino Uno (Rev3) - ICSP

nets:
  VCC: HC-SR04_Sensor_1.VCC, Componente1.5V
  N1: HC-SR04_Sensor_1.TRIG, Componente1.D9_PWM
  N2: HC-SR04_Sensor_1.ECHO, Componente1.D8
  GND: HC-SR04_Sensor_1.GND, Componente1.GND
