# Fritzing sketch Circuito (saved by Fritzing 0.9.5d)
breadboards: 1

parts:
  U1 = ESP32-38PinWide [part_number=ESP32-38PinWide]
  S1 = Pushbutton [package="[THT]"]
  LED1 = LED - 5mm [color="Red (633nm)" package="5 mm [THT]"]
  R1 = Resistor [tolerance=±5% resistance=220 package=THT]
  R2 = Resistor [tolerance=±5% resistance=33 package=THT]

nets:
  N1: U1.3.3, U1.VIN, R1.Pin_0
  N2: U1.GPIO11, S1.Pin_3, S1.Pin_4
  N3: U1.GPIO15, LED1.anode
  N4: U1.GPIO5, S1.Pin_1, S1.Pin_2, R1.Pin_1
  N5: LED1.cathode, R2.Pin_1

custom parts:
  ESP32-38PinWide: Generic 38-Pin ESP32 with wide format (only access to one side of pins on a breadboard) based on Stephen Lilley's HiLetgo ESP-WROOM-32 ESP32 ESP-32S Development Board.
