# Fritzing sketch ArduinoMasBlurtooth (saved by Fritzing 0.9.5d)
breadboards: 1

parts:
  Componente1 = Bluetooth HC-05 Macho
  Componente2 = Arduino Uno (Rev3)
  LED1 = LED - 5mm [color="Red (633nm)" package="5 mm [THT]"]
  R1 = Resistor [tolerance=±5% resistance=330 package=THT]
  LED2 = LED - 5mm [color="Red (633nm)" package="5 mm [THT]"]
  R2 = Resistor [tolerance=±5% resistance=330 package=THT]

nets:
  N1: Componente1.TXD, Componente2.D2
  N2: Componente1.RXD, Componente2.D3_PWM
  VCC: Componente1.VCC, Componente2.5V
  GND: Componente1.GND, Componente2.GND, LED1.cathode, LED2.cathode
  N3: Componente2.D5_PWM, R2.Pin_1
  N4: Componente2.D6_PWM, R1.Pin_1
  N5: LED1.anode, R1.Pin_0
  N6: LED2.anode, R2.Pin_0
