# Fritzing sketch Diagrama (saved by Fritzing 0.9.5d)
breadboards: 1

parts:
  Componente1 = Arduino Uno (Rev3)
  LED3 = LED - 5mm [color="Red (633nm)" package="5 mm [THT]"]
  LED4 = LED - 5mm [color="Red (633nm)" package="5 mm [THT]"]
  R2 = Resistor [tolerance=±5% resistance=220 package=THT]
  R3 = Resistor [tolerance=±5% resistance=220 package=THT]
  LED5 = LED - 5mm [color="Red (633nm)" package="5 mm [THT]"]
  LED6 = LED - 5mm [color="Red (633nm)" package="5 mm [THT]"]
  LED7 = LED - 5mm [color="Red (633nm)" package="5 mm [THT]"]
  LED8 = LED - 5mm [color="Red (633nm)" package="5 mm [THT]"]
  LED9 = LED - 5mm [color="Red (633nm)" package="5 mm [THT]"]
  LED10 = LED - 5mm [color="Red (633nm)" package="5 mm [THT]"]
  LED11 = LED - 5mm [color="Red (633nm)" package="5 mm [THT]"]
  LED12 = LED - 5mm [color="Red (633nm)" package="5 mm [THT]"]
  R4 = Resistor [tolerance=±5% resistance=220 package=THT]
  R5 = Resistor [tolerance=±5% resistance=220 package=THT]
  R6 = Resistor [tolerance=±5% resistance=220 package=THT]
  R7 = Resistor [tolerance=±5% resistance=220 package=THT]
  R8 = Resistor [tolerance=±5% resistance=220 package=THT]
  R9 = Resistor [tolerance=±5% resistance=220 package=THT]
  R10 = Resistor [tolerance=±5% resistance=220 package=THT]
  R11 = Resistor [tolerance=±5% resistance=220 package=THT]
  S1 = Pushbutton [package="[THT]"]
  R12 = Resistor [tolerance=±5% resistance=10k package=THT]

nets:
  N1: Componente1.D8, LED8.anode
  N2: Componente1.D9_PWM, LED9.anode
  N3: Componente1.D10_PWM/SS, LED10.anode
  N4: Componente1.D11_PWM/MOSI, LED11.anode
  N5: Componente1.D12/MISO, LED12.anode
  N6: Componente1.GND, R2.Pin_1, R3.Pin_1, R4.Pin_1, R5.Pin_1, R6.Pin_1, R7.Pin_1, R8.Pin_1, R9.Pin_1, R10.Pin_1, R11.Pin_1, R12.Pin_0
  N7: Componente1.D2, S1.Pin_3, S1.Pin_4, R12.Pin_1
  N8: Componente1.D3_PWM, LED4.anode
  N9: Componente1.D4, LED3.anode
  N10: Componente1.D5_PWM, LED5.anode
  N11: Componente1.D6_PWM, LED6.anode
  N12: Componente1.D7, LED7.anode
  N13: Componente1.5V, S1.Pin_1, S1.Pin_2
  N14: LED3.cathode, R2.Pin_0
  N15: LED4.cathode, R3.Pin_0
  N16: LED5.cathode, R4.Pin_0
  N17: LED6.cathode, R5.Pin_0
  N18: LED7.cathode, R6.Pin_0
  N19: LED8.cathode, R7.Pin_0
  N20: LED9.cathode, R8.Pin_0
  N21: LED10.cathode, R9.Pin_0
  N22: LED11.cathode, R10.Pin_0
  N23: LED12.cathode, R11.Pin_0
