# Fritzing sketch ArduinoBlurtooth (saved by Fritzing 0.9.5d)
breadboards: 1

parts:
  Componente1 = Bluetooth HC-05 Macho
  Componente2 = Arduino Uno (Rev3)
  R1 = Resistor [tolerance=±5% resistance=330 package=THT]
  R3 = Resistor [tolerance=±5% resistance=330 package=THT]
  LED1 = LED - 5mm [color="Red (633nm)" package="5 mm [THT]"]
  LED2 = LED - 5mm [color="Blue (525nm)" package="5 mm [THT]"]

nets:
  N1: Componente1.TXD, Componente2.D2
  N2: Componente1.RXD, Componente2.D3_PWM
  VCC: Componente1.VCC, Componente2.5V
  GND: Componente1.GND, Componente2.GND, R1.Pin_0, R3.Pin_0
  N3: Componente2.D4, LED2.anode
  N4: Componente2.D5_PWM, LED1.anode
  N5: R1.Pin_1, LED1.cathode
  N6: R3.Pin_1, LED2.cathode
