# Fritzing sketch Arduino_Uno_Plotter (saved by Fritzing 0.9.5d)
breadboards: 1

parts:
  Componente1 = Arduino Uno (Rev3)
  S1 = Pushbutton [package="[THT]"]
  S2 = Pushbutton [package="[THT]"]
  S3 = Pushbutton [package="[THT]"]
  R1 = Rotary Potentiometer (Small) [maximum_resistance=100kΩ package=THT]
  R2 = Resistor [tolerance=±5% resistance=10k package=THT]
  R3 = Resistor [tolerance=±5% resistance=10k package=THT]
  R4 = Resistor [tolerance=±5% resistance=10k package=THT]

nets:
  N1: Componente1.A0, R1.wiper
  N2: Componente1.D2, S1.Pin_1, S1.Pin_2, R2.Pin_1
  N3: Componente1.D3_PWM, S2.Pin_1, S2.Pin_2, R3.Pin_1
  N4: Componente1.D4, S3.Pin_1, S3.Pin_2, R4.Pin_1
  N5: Componente1.5V, S1.Pin_3, S1.Pin_4, S2.Pin_3, S2.Pin_4, S3.Pin_3, S3.Pin_4, R1.leg2
  N6: Componente1.GND, R1.leg1, R2.Pin_0, R3.Pin_0, R4.Pin_0
