# Fritzing sketch Boton_Multi_Funciones (saved by Fritzing 1.0.4)
breadboards: 1

parts:
  Componente1 = Arduino Uno (Rev3) - ICSP
  LED1 = LED - 5mm [color="Red (633nm)" current=0.030A package="5 mm [THT]"]
  LED2 = LED - 5mm [color="Blue (525nm)" current=0.030A package="5 mm [THT]"]
  R1 = Resistor [tolerance=±5% power=0.25W resistance=220 package=THT]
  R2 = Resistor [tolerance=±5% power=0.25W resistance=220 package=THT]
  S1 = Pushbutton [package="[THT]"]

nets:
  N1: Componente1.D12/MISO, R2.Pin_1
  N2: Componente1.D13/SCK, R1.Pin_1
  N3: Componente1.D2, S1.Pin_3, S1.Pin_4
  N4: Componente1.GND, LED1.cathode, LED2.cathode, S1.Pin_1, S1.Pin_2
  N5: LED1.anode, R1.Pin_0
  N6: LED2.anode, R2.Pin_0
