# Fritzing sketch SensorPir (saved by Fritzing 0.9.9b)

parts:
  PIR1 = PIR sensor
  Componente1 = Arduino Uno (Rev3)

nets:
  VDD: PIR1.VDD, Componente1.5V
  N1: PIR1.SIG, Componente1.D2
  GND: PIR1.GND, Componente1.GND
