# Fritzing sketch LCD (saved by Fritzing 0.9.9b)
breadboards: 1

parts:
  Componente1 = Arduino Uno (Rev3)
  LCD1 = LCD screen
  R2 = Rotary Potentiometer (Small) [maximum_resistance=100kΩ package=THT]

nets:
  N1: Componente1.D8, LCD1.DB7
  N2: Componente1.D9_PWM, LCD1.DB6
  N3: Componente1.D10_PWM/SS, LCD1.DB5
  N4: Componente1.D11_PWM/MOSI, LCD1.DB4
  N5: Componente1.D12/MISO, LCD1.E
  N6: Componente1.D13/SCK, LCD1.RS
  5V: Componente1.5V, LCD1.VDD, LCD1.LED+, R2.leg1
  GND: Componente1.GND, LCD1.VSS, LCD1.R/W, LCD1.LED-, R2.leg2
  N7: LCD1.V0, R2.wiper
