# Fritzing sketch ConvertidorNivel (saved by Fritzing 1.0.1rc)
breadboards: 2

parts:
  Componente1 = Arduino Uno (Rev3)
  J1 = female pin header, 4 pins [form="♀ (female)"]
  Componente2 = I2C level shifter bidirectional
  Componente4 = I2C level shifter bidirectional
  M1 = DOIT Esp32 DevKit v1 (30 pins long, 11 pins width) [part_number=ESP32S-PIN30]
  KY-1 = Keyes Relay [package=THT]

nets:
  N1: Componente1.D0/RX, Componente2.HV4
  N2: Componente1.D1/TX, Componente2.HV3
  N3: Componente1.3V3, Componente2.LV
  N4: Componente1.5V, J1.pin1, Componente2.HV
  GND: Componente1.GND, J1.pin2, Componente2.GND
  N5: J1.pin3, Componente2.LV3
  N6: J1.pin4, Componente2.LV4
  GND_2: Componente4.GND, M1.GND, KY-1.ground
  N7: Componente4.LV, M1.3V3
  N8: Componente4.HV, M1.VIN, KY-1.power

notes:
  GND
  5V
  RX
  Tx
  5v a 3.3v
  3.3v  a 5v

custom parts:
  DOIT Esp32 DevKit v1 (30 pins long, 11 pins width): The DOIT Esp32 DevKit v1 is one of the development board created by DOIT to evaluate the ESP-WROOM-32 module. It is based on the ESP32 microcontroller that boasts Wifi, Bluetooth, Ethernet and Low Power support all in a single chip. (vanepp) made breadboard work, adjusted pin numbering and labels and reduced size of schematic and cleaned up pcb. This chip is 30pins long (2 x15) and 11 pins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
  Keyes Relay: The Keyes 5V relay module is suitable for SCM development, home appliance control. It uses a 5V~12V TIL control signal which can control DC / AC signal.
