# Fritzing sketch Modulo_Rele (saved by Fritzing 1.0.1rc)
breadboards: 2

parts:
  Componente1 = Arduino Uno (Rev3)
  KY-1 = Keyes Relay [package=THT]
  KY-2 = Keyes Relay [package=THT]
  M1 = DOIT Esp32 DevKit v1 (30 pins long, 11 pins width) [part_number=ESP32S-PIN30]
  R1 = Resistor [tolerance=±5% power=0.25W resistance=330 package=THT]
  R2 = Resistor [tolerance=±5% power=0.25W resistance=10k package=THT]
  Q1 = NPN-Transistor [package="TO92 [THT]"]
  WeMos_D1_Mini1 = WeMos D1 Mini
  KY-3 = Keyes Relay [package=THT]
  Componente2 = I2C level shifter bidirectional

nets:
  N1: Componente1.D13/SCK, KY-1.signal
  N2: Componente1.5V, KY-1.power
  N3: Componente1.GND, KY-1.ground
  N4: KY-2.signal, R2.Pin_0, Q1.B
  N5: KY-2.power, M1.VIN, R2.Pin_1
  N6: KY-2.ground, M1.GND, Q1.E
  N7: M1.D27, R1.Pin_0
  N8: R1.Pin_1, Q1.C
  N9: WeMos_D1_Mini1.3V3, Componente2.LV
  N10: WeMos_D1_Mini1.5V, KY-3.power, Componente2.HV
  N11: WeMos_D1_Mini1.D4, Componente2.LV1
  N12: WeMos_D1_Mini1.G, KY-3.ground, Componente2.GND
  N13: KY-3.signal, Componente2.HV1

custom parts:
  Keyes Relay: The Keyes 5V relay module is suitable for SCM development, home appliance control. It uses a 5V~12V TIL control signal which can control DC / AC signal.
  DOIT Esp32 DevKit v1 (30 pins long, 11 pins width): The DOIT Esp32 DevKit v1 is one of the development board created by DOIT to evaluate the ESP-WROOM-32 module. It is based on the ESP32 microcontroller that boasts Wifi, Bluetooth, Ethernet and Low Power support all in a single chip. (vanepp) made breadboard work, adjusted pin numbering and labels and reduced size of schematic and cleaned up pcb. This chip is 30pins long (2 x15) and 11 pins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
