# Fritzing sketch KEYPAD_DIAGRAMAS (saved by Fritzing 1.0.3b)

parts:
  KEYPAD1 = Membrane Matrix Keypad
  Componente1 = Arduino Uno (Rev3)
  Componente2 = Arduino Uno (Rev3)
  Keypad4x1 = Keypad Membran 4x4
  U1 = ESP32S-HiLetgo [part_number=ESP32S-HiLetgo]
  Keypad4x2 = Keypad Membran 4x4
  Mod1 = Amica NodeMCU DEVKIT 1.0
  Keypad4x3 = Keypad Membran 4x4

nets:
  N1: KEYPAD1.1, Componente1.D9_PWM
  N2: KEYPAD1.2, Componente1.D8
  N3: KEYPAD1.3, Componente1.D7
  N4: KEYPAD1.4, Componente1.D6_PWM
  N5: KEYPAD1.5, Componente1.D5_PWM
  N6: KEYPAD1.6, Componente1.D4
  N7: KEYPAD1.7, Componente1.D3_PWM
  N8: Componente2.D8, Keypad4x1.Pin2
  N9: Componente2.D9_PWM, Keypad4x1.Pin1
  N10: Componente2.D2, Keypad4x1.Pin8
  N11: Componente2.D3_PWM, Keypad4x1.Pin7
  N12: Componente2.D4, Keypad4x1.Pin6
  N13: Componente2.D5_PWM, Keypad4x1.Pin5
  N14: Componente2.D6_PWM, Keypad4x1.Pin4
  N15: Componente2.D7, Keypad4x1.Pin3
  N16: U1.GPIO15, Keypad4x2.Pin8
  N17: U1.GPIO2, Keypad4x2.Pin7
  N18: U1.GPIO4, Keypad4x2.Pin6
  N19: U1.GPIO16, Keypad4x2.Pin5
  N20: U1.GPIO17, Keypad4x2.Pin4
  N21: U1.GPIO5, Keypad4x2.Pin3
  N22: U1.GPIO18, Keypad4x2.Pin2
  N23: U1.GPIO19, Keypad4x2.Pin1
  N24: Mod1.pin6, Keypad4x3.Pin8
  N25: Mod1.pin7, Keypad4x3.Pin7
  N26: Mod1.pin8, Keypad4x3.Pin6
  N27: Mod1.pin_11, Keypad4x3.Pin5
  N28: Mod1.pin_12, Keypad4x3.Pin4
  N29: Mod1.pin_13, Keypad4x3.Pin3
  N30: Mod1.pin_14, Keypad4x3.Pin2
  N31: Mod1.pin_15, Keypad4x3.Pin1

custom parts:
  Membrane Matrix Keypad: Membrane Matrix 3x4 Keypad
  Keypad Membran 4x4: Membrane Keypad 4x4 Matrix
  ESP32S-HiLetgo: HiLetgo ESP-WROOM-32 ESP32 ESP-32S Development Board 2.4GHz Dual-Mode WiFi + Bluetooth Dual Cores Microcontroller The ESP32 integrated with Antenna switches, RF Balun, power amplifiers, low-noise amplifiers, filters, and management modules, and the entire solution occupies the least area of PCB. 2.4 GHz Wi-Fi plus Bluetooth dual-mode chip, with TSMC Ultra-low power consumption 40nm technology,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
