# Fritzing sketch Dagrama DHT11 CON PCB (saved by Fritzing 1.0.3b)
breadboards: 1

parts:
  Componente1 = Arduino Uno (Rev3) - ICSP
  DHT1 = DHT11 Humitidy and Temperature Sensor (3 pins)
  DHT2 = DHT11 Humitidy and Temperature Sensor (3 pins)
  Mod1 = Amica NodeMCU DEVKIT 1.0
  U1 = ESP32S-HiLetgo [part_number=ESP32S-HiLetgo]
  DHT3 = DHT11 Humitidy and Temperature Sensor (3 pins)
  Componente2 = Arduino Uno (Rev3) - ICSP
  DHT4 = Humidity and Temperature Sensor DHT11
  R1 = Resistor [tolerance=±5% power=0.25W resistance=5k package=THT]

nets:
  N1: Componente1.D2, DHT1.Signal
  N2: Componente1.5V, DHT1.Plus
  GND: Componente1.GND, DHT1.Gnd
  N3: DHT2.Plus, Mod1.pin1, Mod1.pin_10
  N4: DHT2.Signal, Mod1.pin6
  N5: DHT2.Gnd, Mod1.pin_9
  N6: U1.3.3, DHT3.Plus
  N7: U1.GPIO4, DHT3.Signal
  GND_2: U1.GND, DHT3.Gnd
  N8: Componente2.D2, DHT4.Data-signal, R1.Pin_0
  5V: Componente2.5V, DHT4.Vcc, R1.Pin_1
  N9: Componente2.GND, DHT4.GND_2

custom parts:
  DHT11 Humitidy and Temperature Sensor (3 pins): DHT11 Humidity and Temperature Sensor (3 pins).
  ESP32S-HiLetgo: HiLetgo ESP-WROOM-32 ESP32 ESP-32S Development Board 2.4GHz Dual-Mode WiFi + Bluetooth Dual Cores Microcontroller The ESP32 integrated with Antenna switches, RF Balun, power amplifiers, low-noise amplifiers, filters, and management modules, and the entire solution occupies the least area of PCB. 2.4 GHz Wi-Fi plus Bluetooth dual-mode chip, with TSMC Ultra-low power consumption 40nm technology,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
  Humidity and Temperature Sensor DHT11: Digital relative humidity & temperature sensor DHT11
