# Fritzing sketch DiagramaWebServerNeopixel_v2 (saved by Fritzing 1.0.1rc)
breadboards: 1

parts:
  NEOPIXEL1 = Neopixel Strip -- Black (30/m)
  NEOPIXEL2 = Neopixel Strip -- Black (30/m)
  M1 = DOIT Esp32 DevKit v1 (30 pins long, 11 pins width) [part_number=ESP32S-PIN30]
  R1 = Resistor [tolerance=±5% power=0.25W resistance=220 package=THT]
  NEOPIXEL3 = Neopixel Strip -- Black (30/m)
  NEOPIXEL4 = Neopixel Strip -- Black (30/m)
  R2 = Resistor [tolerance=±5% power=0.25W resistance=220 package=THT]
  R3 = Resistor [tolerance=±5% power=0.25W resistance=220 package=THT]
  R4 = Resistor [tolerance=±5% power=0.25W resistance=220 package=THT]
  LED1 = smd LED [color="Red (633nm)" current=0.030A package="0603 [SMD]"]
  R5 = Resistor [tolerance=±5% power=0.25W resistance=330 package=THT]
  S1 = Pushbutton [package="[THT]"]
  R6 = Resistor [tolerance=±5% power=0.25W resistance=10k package=THT]
  C1 = Electrolytic Capacitor [capacitance=1µF voltage=35V package="100 mil [THT, electrolytic]"]
  U1 = Mini-360 DC-DC Buck converter [package=THT]
  J1 = 220v plug
  S2 = Toggle Switch [package=THT]

nets:
  +5V: NEOPIXEL1.+5V, NEOPIXEL2.+5V, NEOPIXEL3.+5V, NEOPIXEL4.+5V, C1.+, U1.OUT+, S2.L2
  N1: NEOPIXEL1.DI, R3.Pin_1
  GND: NEOPIXEL1.GND, NEOPIXEL2.GND, M1.GND, NEOPIXEL3.GND, NEOPIXEL4.GND, R5.Pin_0, R6.Pin_0, C1.-, U1.OUT-
  N2: NEOPIXEL2.DI, R4.Pin_1
  N3: M1.3V3, S1.Pin_1, S1.Pin_2
  N4: M1.D2, LED1.cathode
  N5: M1.D4, R1.Pin_0
  N6: M1.D5, R2.Pin_0
  N7: M1.D18, R3.Pin_0
  N8: M1.D19, R4.Pin_0
  N9: M1.D22, S1.Pin_3, S1.Pin_4, R6.Pin_1
  N10: M1.VIN, S2.COM
  N11: R1.Pin_1, NEOPIXEL4.DI
  N12: NEOPIXEL3.DI, R2.Pin_1
  N13: LED1.anode, R5.Pin_1
  N14: U1.IN-, J1.pin1
  N15: U1.IN+, J1.pin2

custom parts:
  Neopixel Strip -- Black (30/m): Neopixel Strip, Black, 30 pixels per meter.
  DOIT Esp32 DevKit v1 (30 pins long, 11 pins width): The DOIT Esp32 DevKit v1 is one of the development board created by DOIT to evaluate the ESP-WROOM-32 module. It is based on the ESP32 microcontroller that boasts Wifi, Bluetooth, Ethernet and Low Power support all in a single chip. (vanepp) made breadboard work, adjusted pin numbering and labels and reduced size of schematic and cleaned up pcb. This chip is 30pins long (2 x15) and 11 pins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
  Mini-360 DC-DC Buck converter: Mini-360 DC-DC Buck converter. Tiny buck step down voltage converter, input voltage 4.75 to 23V output 1 to 17V adjustable. Available from ebay and the like.
  220v plug: Generic 220V AC plug.
