# Fritzing sketch Ejemplo_01 (saved by Fritzing 0.9.9b)
breadboards: 1

parts:
  Componente1 = Bluetooth HC-05 Macho
  Componente2 = Arduino Uno (Rev3)
  LED1 = LED - 5mm [color="Red (633nm)" current=0.030 package="5 mm [THT]"]
  LED2 = LED - 5mm [color="Red (633nm)" current=0.030 package="5 mm [THT]"]
  LED3 = LED - 5mm [color="Red (633nm)" current=0.030 package="5 mm [THT]"]
  LED4 = LED - 5mm [color="Red (633nm)" current=0.030 package="5 mm [THT]"]
  LED5 = LED - 5mm [color="Red (633nm)" current=0.030 package="5 mm [THT]"]
  LED6 = LED - 5mm [color="Red (633nm)" current=0.030 package="5 mm [THT]"]
  LED7 = LED - 5mm [color="Red (633nm)" current=0.030 package="5 mm [THT]"]
  LED8 = LED - 5mm [color="Red (633nm)" current=0.030 package="5 mm [THT]"]
  LED9 = LED - 5mm [color="Red (633nm)" current=0.030 package="5 mm [THT]"]
  LED10 = LED - 5mm [color="Red (633nm)" current=0.030 package="5 mm [THT]"]
  R1 = Resistor [tolerance=±5% power=0.25 resistance=330 package=THT]
  R2 = Resistor [tolerance=±5% power=0.25 resistance=330 package=THT]
  R3 = Resistor [tolerance=±5% power=0.25 resistance=330 package=THT]
  R4 = Resistor [tolerance=±5% power=0.25 resistance=330 package=THT]
  R5 = Resistor [tolerance=±5% power=0.25 resistance=330 package=THT]
  R6 = Resistor [tolerance=±5% power=0.25 resistance=330 package=THT]
  R7 = Resistor [tolerance=±5% power=0.25 resistance=330 package=THT]
  R8 = Resistor [tolerance=±5% power=0.25 resistance=330 package=THT]
  R9 = Resistor [tolerance=±5% power=0.25 resistance=330 package=THT]
  R10 = Resistor [tolerance=±5% power=0.25 resistance=330 package=THT]

nets:
  N1: Componente1.TXD, Componente2.D2
  N2: Componente1.RXD, Componente2.D3_PWM
  VCC: Componente1.VCC, Componente2.5V
  GND: Componente1.GND, Componente2.GND, LED1.cathode, LED2.cathode, LED3.cathode, LED4.cathode, LED5.cathode, LED6.cathode, LED7.cathode, LED8.cathode, LED9.cathode, LED10.cathode
  N3: Componente2.D8, R5.Pin_1
  N4: Componente2.D9_PWM, R2.Pin_1
  N5: Componente2.D10_PWM/SS, R4.Pin_1
  N6: Componente2.D11_PWM/MOSI, R3.Pin_1
  N7: Componente2.D12/MISO, R6.Pin_1
  N8: Componente2.D13/SCK, R1.Pin_1
  N9: Componente2.D4, R10.Pin_1
  N10: Componente2.D5_PWM, R9.Pin_1
  N11: Componente2.D6_PWM, R8.Pin_1
  N12: Componente2.D7, R7.Pin_1
  N13: LED1.anode, R1.Pin_0
  N14: LED2.anode, R6.Pin_0
  N15: LED3.anode, R3.Pin_0
  N16: LED4.anode, R4.Pin_0
  N17: LED5.anode, R2.Pin_0
  N18: LED6.anode, R5.Pin_0
  N19: LED7.anode, R7.Pin_0
  N20: LED8.anode, R8.Pin_0
  N21: LED9.anode, R9.Pin_0
  N22: LED10.anode, R10.Pin_0
