# Fritzing sketch TecladoBLE_ESP32 (saved by Fritzing 1.0.1rc)
breadboards: 1

parts:
  R1 = Resistor [tolerance=±5% power=0.25W resistance=10k package=THT]
  S1 = Pushbutton [package="[THT]"]
  M1 = DOIT Esp32 DevKit v1 (30 pins long, 11 pins width) [part_number=ESP32S-PIN30]

nets:
  N1: R1.Pin_0, S1.Pin_1, S1.Pin_2, M1.D15
  N2: R1.Pin_1, M1.GND
  N3: S1.Pin_3, S1.Pin_4, M1.3V3

custom parts:
  DOIT Esp32 DevKit v1 (30 pins long, 11 pins width): The DOIT Esp32 DevKit v1 is one of the development board created by DOIT to evaluate the ESP-WROOM-32 module. It is based on the ESP32 microcontroller that boasts Wifi, Bluetooth, Ethernet and Low Power support all in a single chip. (vanepp) made breadboard work, adjusted pin numbering and labels and reduced size of schematic and cleaned up pcb. This chip is 30pins long (2 x15) and 11 pins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
