# Fritzing sketch Diagrama (saved by Fritzing 0.9.5d)
circuit board: 6.88566cm x 5.36311cm
breadboards: 1

parts:
  Arduino_UNO = Arduino Uno (Rev3)
  L_Amarillo = LED - 5mm [color="Yellow (595nm)" package="5 mm [THT]"]
  R_Amarillo = Resistor [tolerance=±5% resistance=220 package=THT]
  R_Volumen = TRIMPOT [package=trimpot_pth_s3_lock]
  B_Amarillo = Pushbutton [package="[THT]"]
  B_Azul = Pushbutton [package="[THT]"]
  B_Verde = Pushbutton [package="[THT]"]
  B_Rojo = Pushbutton [package="[THT]"]
  Buzzer = Buzzer 12mm [package=buzzer-12mm-ns]
  L_Azul = LED - 5mm [color="Blue (505nm)" package="5 mm [THT]"]
  L_Verde = LED - 5mm [color="Green (570nm)" package="5 mm [THT]"]
  R_Azul = Resistor [tolerance=±5% resistance=220 package=THT]
  R_Verde = Resistor [tolerance=±5% resistance=220 package=THT]
  R_Rojo = Resistor [tolerance=±5% resistance=220 package=THT]
  R_Velocidad = TRIMPOT [package=trimpot_pth_s3_lock]
  L_Rojo = LED - 5mm [color="Red (660nm)" package="5 mm [THT]"]

nets:
  Velocidad: Arduino_UNO.A0, R_Velocidad.WIPER
  Led_Amarillo: Arduino_UNO.D8, L_Amarillo.anode
  B_Amarillo: Arduino_UNO.D9_PWM, B_Amarillo.Pin_1, B_Amarillo.Pin_2
  Buzzer: Arduino_UNO.D10_PWM/SS, Buzzer.1
  Led_Rojo: Arduino_UNO.D2, L_Rojo.anode
  B_Rojo: Arduino_UNO.D3_PWM, B_Rojo.Pin_1, B_Rojo.Pin_2
  Led_Verde: Arduino_UNO.D4, L_Verde.anode
  B_Verde: Arduino_UNO.D5_PWM, B_Verde.Pin_1, B_Verde.Pin_2
  Led_Azul: Arduino_UNO.D6_PWM, L_Azul.anode
  B_Azul: Arduino_UNO.D7, B_Azul.Pin_1, B_Azul.Pin_2
  5V: Arduino_UNO.5V, R_Velocidad.CCW
  GND: Arduino_UNO.GND, R_Amarillo.Pin_1, R_Volumen.WIPER, B_Amarillo.Pin_3, B_Amarillo.Pin_4, B_Azul.Pin_3, B_Azul.Pin_4, B_Verde.Pin_3, B_Verde.Pin_4, B_Rojo.Pin_3, B_Rojo.Pin_4, R_Azul.Pin_1, R_Verde.Pin_1, R_Rojo.Pin_1, R_Velocidad.CW
  N1: L_Amarillo.cathode, R_Amarillo.Pin_0
  N2: R_Volumen.CW, Buzzer.2
  N3: L_Azul.cathode, R_Azul.Pin_0
  N4: L_Verde.cathode, R_Verde.Pin_0
  N5: R_Rojo.Pin_0, L_Rojo.cathode

notes:
  Simon Dice por ChepeCarloss, NocheProgramacion.com/simon_dice, 0.1

custom parts:
  Pushbutton: A generic pushbutton.
  Pushbutton: A generic pushbutton.
  Pushbutton: A generic pushbutton.
  Pushbutton: A generic pushbutton.
  Buzzer 12mm: Buzzer 12mm Spark Fun Electronics SKU : Comp-Buzzer Through hole
