# Fritzing sketch AlexaRele (saved by Fritzing 0.9.3b)
circuit board: 4.45524cm x 3.97982cm
breadboards: 1

parts:
  Componente1 = SparkFun ESP8266 Thing
  J1 = female pin header, 3 pins [form="♀ (female)"]
  Q1 = NPN-Transistor [package="TO92 [THT]"]
  R1 = Resistor [tolerance=±5% resistance=10k package=THT]
  R2 = Resistor [tolerance=±5% resistance=220 package=THT]

nets:
  N1: Componente1.GND, J1.pin2, Q1.E
  N2: Componente1.GPIO14, R2.Pin_0
  N3: Componente1.USBVCC, J1.pin3, R1.Pin_0
  N4: J1.pin1, Q1.C, R1.Pin_1
  N5: Q1.B, R2.Pin_1

notes:
  Señal
  GND
  Rele
  Vcc
